# Fritzing sketch particle-power-monitor (saved by Fritzing 0.9.2b)
breadboards: 1

parts:
  Part1 = Spark Core (v1.0)
  U1 = LIPO-110mAh [package=lipo-110]
  R1 = Resistor [tolerance=±5% resistance=330 package=THT]
  R2 = Resistor [tolerance=±5% resistance=220 package=THT]
  Part2 = Power Cell LiPo Charger/Booster

nets:
  GND: Part1.GND, U1.-, R2.Pin_1, Part2.GND
  N1: Part1.VIN, Part2.5VIN
  N2: Part1.D7, R1.Pin_1, R2.Pin_0
  N3: U1.+, Part2.VBATT
  N4: R1.Pin_0, Part2.VCC
